# Fritzing sketch schematic (saved by Fritzing 0.9.4)
breadboards: 1

parts:
  Raspberry_Pi_5_8GB = Raspberry Pi B+
  MCP3008 = MCP3008 [package=dil16]
  S1 = Momentary Switch [package=tactile-pth]
  R1 = Resistor [tolerance=±5% resistance=470 package="0805 [SMD]"]
  R2 = Trimmer Potentiometer [maximum_resistance=10kΩ package=THT]
  DS1 = DS18B20 1-Wire Temperature Sensor [part_number=DS18B20]
  R3 = Resistor [tolerance=±5% resistance=4.7k package="0805 [SMD]"]
  R4 = Photocell (LDR) [package=THT]
  R5 = Resistor [tolerance=±5% resistance=10k package="0805 [SMD]"]
  R6 = Resistor [tolerance=±5% resistance=470 package="0805 [SMD]"]
  Reed_switch = SWITCH-MOMENTARY-2 [package=reed_switch_pth]
  IR1 = TSOP312.., 314.. [package=THT]
  D2 = SOLAR-IXYS [package=solarbit-12x1]  # not connected
  Powerbank_5V = BC9VPC [package=bc9vpc]
  INA1 = INA219 DC Current Sensor Breakout
  RFID = RFID-RC522-v2
  LED1O = LEDs [package=led10mm]
  LED2O = LEDs [package=led10mm]
  LED3O = LEDs [package=led10mm]
  LED1L = LEDs [package=led10mm]
  FAN = DC Motor
  LED1B = LEDs [package=led10mm]
  INA2 = INA219 DC Current Sensor Breakout
  INA3 = INA219 DC Current Sensor Breakout
  INA4 = INA219 DC Current Sensor Breakout
  Heating_element = Resistor [tolerance=±5% resistance=10 package="2512 [SMD]"]
  Q1 = TRANSISTOR_NPN [package=to-92]
  Q2 = TRANSISTOR_NPN [package=to-92]
  5V_TO_3V3 = Transformer [package=transformer_smd]
  R7 = Resistor [tolerance=±5% resistance=100 package="2512 [SMD]"]
  R8 = Resistor [tolerance=±5% resistance=100 package="2512 [SMD]"]
  R9 = Resistor [tolerance=±5% resistance=100 package="0805 [SMD]"]
  R10 = Resistor [tolerance=±5% resistance=100 package="0805 [SMD]"]
  R11 = Resistor [tolerance=±5% resistance=100 package="0805 [SMD]"]

nets:
  N1: Raspberry_Pi_5_8GB.GPIO2, INA1.SDA, INA2.SDA, INA3.SDA, INA4.SDA
  N2: Raspberry_Pi_5_8GB.GPIO3, INA1.SCL, INA2.SCL, INA3.SCL, INA4.SCL
  N3: Raspberry_Pi_5_8GB.GPIO4, DS1.DQ, R3.Pin_1
  N4: Raspberry_Pi_5_8GB.GPIO10, MCP3008.Dout, RFID.MOSI
  N5: Raspberry_Pi_5_8GB.GPIO9, MCP3008.Din, RFID.MISO
  N6: Raspberry_Pi_5_8GB.GPIO11, MCP3008.CLK, RFID.SCK
  GND: Raspberry_Pi_5_8GB.GND, MCP3008.DGND, MCP3008.AGND, S1.1, R2.leg2, DS1.GND, R4.pin_0, Reed_switch.1, IR1.GND, Powerbank_5V.V-, INA1.GND, RFID.RST, INA2.GND, INA3.GND, INA4.GND, Heating_element.Pin_1, 5V_TO_3V3.2, 5V_TO_3V3.4
  N7: Raspberry_Pi_5_8GB.GPIO13, IR1.Data
  N8: Raspberry_Pi_5_8GB.GPIO19, R6.Pin_0, Reed_switch.2
  N9: Raspberry_Pi_5_8GB.GPIO26, S1.3, R1.Pin_0
  N10: Raspberry_Pi_5_8GB.GPIO20, R7.Pin_0
  N11: Raspberry_Pi_5_8GB.GPIO16, R8.Pin_0
  N12: Raspberry_Pi_5_8GB.GPIO12, INA2.Vin+
  N13: Raspberry_Pi_5_8GB.GPIO7, RFID.SDA
  N14: Raspberry_Pi_5_8GB.GPIO8, MCP3008.CS/SHDN
  N15: Raspberry_Pi_5_8GB.GPIO25, RFID.GND
  N16: Raspberry_Pi_5_8GB.GPIO24, LED1B.A
  N17: Raspberry_Pi_5_8GB.GPIO23, INA1.Vin+
  N18: MCP3008.CH0, R2.wiper
  N19: MCP3008.CH1, R4.pin_1, R5.Pin_1
  VCC: MCP3008.VREF, MCP3008.VDD, R2.leg1, DS1.VDD, R3.Pin_0, R5.Pin_0, R6.Pin_1, INA1.VCC, RFID.3.3V, INA2.VCC, INA3.VCC, INA4.VCC, 5V_TO_3V3.3
  N20: IR1.Vs, Powerbank_5V.V+, INA3.Vin+, INA4.Vin+, 5V_TO_3V3.1
  N21: INA1.Vin-, LED1O.A, LED2O.A, LED3O.A
  N22: LED1O.C, R9.Pin_0
  N23: LED2O.C, R11.Pin_0
  N24: LED3O.C, R10.Pin_0
  N25: LED1L.C, FAN.pin_2, LED1B.C, R9.Pin_1, R10.Pin_1, R11.Pin_1
  N26: LED1L.A, INA2.Vin-
  N27: FAN.pin_1, Q1.E
  N28: INA3.Vin-, Q1.C
  N29: INA4.Vin-, Q2.C
  N30: Heating_element.Pin_0, Q2.E
  N31: Q1.B, R8.Pin_1
  N32: Q2.B, R7.Pin_1

custom parts:
  INA219 DC Current Sensor Breakout: INA DC Current Sensor Breakout
  RFID-RC522-v2: A simple China made RFID-RC522 Reader; do check the pin labels, as this is a MFRC522 based clone.
